# Fritzing sketch SmartGas (saved by Fritzing 0.9.3b)
breadboards: 1

parts:
  U1 = ESP32S-HiLetgo [part_number=ESP32S-HiLetgo]
  MQ2 = MQ-4
  Buzzer = Passive Buzzer
  Ventilador = Fan - Ventilador [package=THT]
  LED = RGB LED (com. cathode, rgb) [package="5 mm [THT]"]
  Servo = Basic Servo

nets:
  N1: U1.3.3, Buzzer.NC
  N2: U1.GPIO36, MQ2.AO
  N3: U1.GPIO33, Servo.pulse
  GND: U1.GND, MQ2.GND, Buzzer.GND, Ventilador.GND, LED.common_cathode, Servo.gnd
  VCC: U1.VIN, MQ2.VCC, Ventilador.5V, Servo.vcc
  N4: U1.GPIO5, Buzzer.S
  N5: U1.GPIO21, LED.blue_anode
  N6: U1.GPIO22, LED.green_anode
  N7: U1.GPIO23, LED.red_anode

notes:
  Acá va el buzzer pero no tiene esquematico

custom parts:
  ESP32S-HiLetgo: HiLetgo ESP-WROOM-32 ESP32 ESP-32S Development Board 2.4GHz Dual-Mode WiFi + Bluetooth Dual Cores Microcontroller The ESP32 integrated with Antenna switches, RF Balun, power amplifiers, low-noise amplifiers, filters, and management modules, and the entire solution occupies the least area of PCB. 2.4 GHz Wi-Fi plus Bluetooth dual-mode chip, with TSMC Ultra-low power consumption 40nm technology,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
  Fan - Ventilador: Ventilador de 2 pines, se encuentra comunmente en computadoras de escritorio
